// Logisim project counter schema.circ as structural Verilog: 6 circuits, main circuit main
module main (
);

  wire and_1_out, and_2_out, and_3_out, and_4_out, and_5_out, not_1_out, not_2_out, not_3_out, not_4_out,
       not_5_out, not_6_out, or_1_out, P_out, t_ff_1_q, t_ff_2_q, t_ff_3_q, t_ff_4_q;

  Button P (.out(P_out));
  or or_1 (or_1_out, t_ff_1_q, and_5_out);
  and and_1 (and_1_out, P_out, or_1_out);
  and and_2 (and_2_out, and_1_out, t_ff_2_q);
  and and_3 (and_3_out, t_ff_3_q, and_2_out);
  not not_1 (not_1_out, P_out);
  buf and_4 (and_4_out, not_2_out);  // AND_Gate
  not not_2 (not_2_out, and_5_out);
  not not_3 (not_3_out, and_1_out);
  not not_4 (not_4_out, and_2_out);
  not not_5 (not_5_out, and_3_out);
  T_Flip_Flop t_ff_1 (.clk(not_1_out), .T(and_4_out), .Q(t_ff_1_q));  // open: Qn, preset, reset, en
  T_Flip_Flop t_ff_2 (.clk(not_3_out), .T(1'b1), .Q(t_ff_2_q));  // open: Qn, preset, reset, en
  T_Flip_Flop t_ff_3 (.clk(not_4_out), .T(1'b1), .Q(t_ff_3_q));  // open: Qn, preset, reset, en
  T_Flip_Flop t_ff_4 (.clk(not_5_out), .T(1'b1), .Q(t_ff_4_q));  // open: Qn, preset, reset, en
  not not_6 (not_6_out, t_ff_1_q);
  and and_5 (and_5_out, not_6_out, t_ff_2_q, t_ff_3_q, t_ff_4_q);
endmodule

module ttrigger (
  input  I,
  input  T,
  input  Sync,
  output out_4,
  output out_5
);

  jktrigger jktrigger_1 (.in_1(I), .out_4(out_4), .in_3(Sync), .out_5(out_5), .in_2(T));
endmodule

module rstrigger (
  input  R,
  input  Sync,
  input  S,
  input  I,
  output nQ,
  output Q
);

  wire and_1_out, and_2_out, not_1_out, not_2_out;

  and and_1 (and_1_out, R, Sync);
  and and_2 (and_2_out, Sync, S);
  or or_1 (nQ, and_1_out, not_1_out);
  not not_1 (not_1_out, Q);
  not not_2 (not_2_out, nQ);
  or or_2 (Q, not_2_out, and_2_out, I);
endmodule

module jktrigger (
  input  in_1,
  input  in_2,
  input  in_3,
  output out_4,
  output out_5
);

  wire and_1_out, and_2_out, not_1_out, not_2_out, rstrigger_1_nq, rstrigger_1_q;

  not not_1 (not_1_out, in_3);
  and and_1 (and_1_out, out_4, in_2);
  and and_2 (and_2_out, in_2, out_5);
  rstrigger rstrigger_1 (
    .I(in_1), .R(and_1_out), .S(and_2_out), .nQ(rstrigger_1_nq), .Q(rstrigger_1_q), .Sync(not_1_out));
  rstrigger rstrigger_2 (.I(in_1), .R(rstrigger_1_q), .S(rstrigger_1_nq), .nQ(out_5), .Q(out_4), .Sync(not_2_out));
  not not_2 (not_2_out, not_1_out);
endmodule

module counter (
  input  I
);

  wire and_1_out, and_2_out, and_3_out, and_4_out, and_5_out, not_1_out, not_2_out, or_1_out, P_out,
       test_1_out_4, test_2_out_4, test_3_out_4, test_4_out_4;

  Button P (.out(P_out));
  or or_1 (or_1_out, test_1_out_4, and_5_out);
  and and_1 (and_1_out, P_out, or_1_out);
  and and_2 (and_2_out, and_1_out, test_2_out_4);
  and and_3 (and_3_out, test_3_out_4, and_2_out);
  buf and_4 (and_4_out, not_1_out);  // AND_Gate
  not not_1 (not_1_out, and_5_out);
  test test_1 (.in_1(I), .in_2(and_4_out), .in_3(P_out), .out_4(test_1_out_4));  // open: out_5
  test test_2 (.in_1(I), .in_2(1'b1), .in_3(and_1_out), .out_4(test_2_out_4));  // open: out_5
  test test_3 (.in_1(I), .in_2(1'b1), .in_3(and_2_out), .out_4(test_3_out_4));  // open: out_5
  LED O3 (.in(test_3_out_4));
  test test_4 (.in_1(I), .in_2(1'b1), .in_3(and_3_out), .out_4(test_4_out_4));  // open: out_5
  LED O1 (.in(test_1_out_4));
  LED O2 (.in(test_2_out_4));
  LED O4 (.in(test_4_out_4));
  not not_2 (not_2_out, test_1_out_4);
  and and_5 (and_5_out, not_2_out, test_2_out_4, test_3_out_4, test_4_out_4);
endmodule

module test (
  input  in_1,
  input  in_2,
  input  in_3,
  output out_4,
  output out_5
);

  wire and_1_out, and_2_out, not_1_out, rstrigger_1_nq, rstrigger_1_q;

  and and_1 (and_1_out, out_5, in_2);
  and and_2 (and_2_out, in_2, out_4);
  rstrigger rstrigger_1 (.I(in_1), .R(and_1_out), .S(and_2_out), .nQ(rstrigger_1_nq), .Q(rstrigger_1_q), .Sync(in_3));
  not not_1 (not_1_out, in_3);
  rstrigger rstrigger_2 (.I(in_1), .R(rstrigger_1_q), .S(rstrigger_1_nq), .nQ(out_5), .Q(out_4), .Sync(not_1_out));
endmodule
