// Logisim project root.circ as structural Verilog: 8 circuits, main circuit main
module main (
  input  in_1,
  input  in_2,
  input  in_3,
  input  in_4,
  input  in_5,
  input  in_6,
  input  in_7,
  input  in_8,
  output out_9,
  output out_10,
  output out_11,
  output out_12,
  output out_13,
  output out_14,
  output out_15,
  output out_16
);

  wire next_sqrt_bit_1_out_17, next_sqrt_bit_1_out_18, next_sqrt_bit_1_out_19, next_sqrt_bit_1_out_20,
       next_sqrt_bit_1_out_21, next_sqrt_bit_1_out_22, next_sqrt_bit_1_out_23, next_sqrt_bit_1_out_24,
       next_sqrt_bit_2_out_17, next_sqrt_bit_2_out_18, next_sqrt_bit_2_out_19, next_sqrt_bit_2_out_20,
       next_sqrt_bit_2_out_21, next_sqrt_bit_2_out_22, next_sqrt_bit_2_out_23, next_sqrt_bit_2_out_24,
       next_sqrt_bit_3_out_17, next_sqrt_bit_3_out_18, next_sqrt_bit_3_out_19, next_sqrt_bit_3_out_20,
       next_sqrt_bit_3_out_21, next_sqrt_bit_3_out_22, next_sqrt_bit_3_out_23, next_sqrt_bit_3_out_24,
       not_1_out;

  not not_1 (not_1_out, 1'b1);
  next_sqrt_bit next_sqrt_bit_1 (
    .in_1(not_1_out), .in_2(not_1_out), .in_3(not_1_out), .in_4(not_1_out), .in_5(not_1_out),
    .in_7(not_1_out), .in_9(in_1), .in_11(in_2), .out_17(next_sqrt_bit_1_out_17),
    .out_18(next_sqrt_bit_1_out_18), .out_19(next_sqrt_bit_1_out_19), .out_20(next_sqrt_bit_1_out_20),
    .out_21(next_sqrt_bit_1_out_21), .out_22(next_sqrt_bit_1_out_22), .out_23(next_sqrt_bit_1_out_23),
    .out_24(next_sqrt_bit_1_out_24), .in_6(not_1_out), .in_8(not_1_out), .in_10(not_1_out),
    .in_12(not_1_out), .in_13(not_1_out), .in_14(not_1_out), .in_15(not_1_out), .in_16(not_1_out));
  next_sqrt_bit next_sqrt_bit_2 (
    .in_1(not_1_out), .in_2(not_1_out), .in_3(not_1_out), .in_4(not_1_out), .in_5(in_1), .in_7(in_2),
    .in_9(in_3), .in_11(in_4), .out_17(next_sqrt_bit_2_out_17), .out_18(next_sqrt_bit_2_out_18),
    .out_19(next_sqrt_bit_2_out_19), .out_20(next_sqrt_bit_2_out_20), .out_21(next_sqrt_bit_2_out_21),
    .out_22(next_sqrt_bit_2_out_22), .out_23(next_sqrt_bit_2_out_23), .out_24(next_sqrt_bit_2_out_24),
    .in_6(next_sqrt_bit_1_out_17), .in_8(next_sqrt_bit_1_out_18), .in_10(next_sqrt_bit_1_out_19),
    .in_12(next_sqrt_bit_1_out_20), .in_13(next_sqrt_bit_1_out_21), .in_14(next_sqrt_bit_1_out_22),
    .in_15(next_sqrt_bit_1_out_23), .in_16(next_sqrt_bit_1_out_24));
  next_sqrt_bit next_sqrt_bit_3 (
    .in_1(not_1_out), .in_2(not_1_out), .in_3(in_1), .in_4(in_2), .in_5(in_3), .in_7(in_4), .in_9(in_5),
    .in_11(in_6), .out_17(next_sqrt_bit_3_out_17), .out_18(next_sqrt_bit_3_out_18),
    .out_19(next_sqrt_bit_3_out_19), .out_20(next_sqrt_bit_3_out_20), .out_21(next_sqrt_bit_3_out_21),
    .out_22(next_sqrt_bit_3_out_22), .out_23(next_sqrt_bit_3_out_23), .out_24(next_sqrt_bit_3_out_24),
    .in_6(next_sqrt_bit_2_out_17), .in_8(next_sqrt_bit_2_out_18), .in_10(next_sqrt_bit_2_out_19),
    .in_12(next_sqrt_bit_2_out_20), .in_13(next_sqrt_bit_2_out_21), .in_14(next_sqrt_bit_2_out_22),
    .in_15(next_sqrt_bit_2_out_23), .in_16(next_sqrt_bit_2_out_24));
  next_sqrt_bit next_sqrt_bit_4 (
    .in_1(in_1), .in_2(in_2), .in_3(in_3), .in_4(in_4), .in_5(in_5), .in_7(in_6), .in_9(in_7), .in_11(in_8),
    .out_17(out_9), .out_18(out_10), .out_19(out_11), .out_20(out_12), .out_21(out_13), .out_22(out_14),
    .out_23(out_15), .out_24(out_16), .in_6(next_sqrt_bit_3_out_17), .in_8(next_sqrt_bit_3_out_18),
    .in_10(next_sqrt_bit_3_out_19), .in_12(next_sqrt_bit_3_out_20), .in_13(next_sqrt_bit_3_out_21),
    .in_14(next_sqrt_bit_3_out_22), .in_15(next_sqrt_bit_3_out_23), .in_16(next_sqrt_bit_3_out_24));
endmodule

module cmp (
  input  in_1,
  input  in_2,
  input  in_3,
  input  in_4,
  input  in_5,
  input  in_6,
  input  in_7,
  input  in_8,
  input  in_9,
  input  in_10,
  input  in_11,
  input  in_12,
  input  in_13,
  input  in_14,
  input  in_15,
  input  in_16,
  input  in_17,
  input  in_18,
  input  in_19,
  input  in_20,
  output out_21
);

  wire cmp_node_1_out_4, cmp_node_1_out_5, cmp_node_2_out_4, cmp_node_2_out_5, cmp_node_3_out_4,
       cmp_node_3_out_5, cmp_node_4_out_4, cmp_node_4_out_5, cmp_node_5_out_4, cmp_node_5_out_5,
       cmp_node_6_out_4, cmp_node_6_out_5, cmp_node_7_out_4, cmp_node_7_out_5, cmp_node_8_out_4,
       cmp_node_8_out_5, cmp_node_9_out_4, cmp_node_9_out_5, cmp_node_10_out_4, not_1_out;

  cmp_node cmp_node_1 (.in_1(not_1_out), .in_2(in_1), .in_3(in_2), .out_4(cmp_node_1_out_4), .out_5(cmp_node_1_out_5));
  not not_1 (not_1_out, 1'b1);
  cmp_node cmp_node_2 (
    .in_1(cmp_node_1_out_5), .in_2(in_3), .in_3(in_4), .out_4(cmp_node_2_out_4), .out_5(cmp_node_2_out_5));
  cmp_node cmp_node_3 (
    .in_1(cmp_node_2_out_5), .in_2(in_5), .in_3(in_6), .out_4(cmp_node_3_out_4), .out_5(cmp_node_3_out_5));
  cmp_node cmp_node_4 (
    .in_1(cmp_node_3_out_5), .in_2(in_7), .in_3(in_8), .out_4(cmp_node_4_out_4), .out_5(cmp_node_4_out_5));
  cmp_node cmp_node_5 (
    .in_1(cmp_node_4_out_5), .in_2(in_9), .in_3(in_10), .out_4(cmp_node_5_out_4), .out_5(cmp_node_5_out_5));
  cmp_node cmp_node_6 (
    .in_1(cmp_node_5_out_5), .in_2(in_11), .in_3(in_12), .out_4(cmp_node_6_out_4), .out_5(cmp_node_6_out_5));
  cmp_node cmp_node_7 (
    .in_1(cmp_node_6_out_5), .in_2(in_13), .in_3(in_14), .out_4(cmp_node_7_out_4), .out_5(cmp_node_7_out_5));
  cmp_node cmp_node_8 (
    .in_1(cmp_node_7_out_5), .in_2(in_15), .in_3(in_16), .out_4(cmp_node_8_out_4), .out_5(cmp_node_8_out_5));
  cmp_node cmp_node_9 (
    .in_1(cmp_node_8_out_5), .in_2(in_17), .in_3(in_18), .out_4(cmp_node_9_out_4), .out_5(cmp_node_9_out_5));
  cmp_node cmp_node_10 (.in_1(cmp_node_9_out_5), .in_2(in_19), .in_3(in_20), .out_4(cmp_node_10_out_4));  // open: out_5
  or or_1 (out_21, cmp_node_1_out_4, cmp_node_2_out_4, cmp_node_3_out_4, cmp_node_4_out_4, cmp_node_5_out_4, cmp_node_6_out_4, cmp_node_7_out_4, cmp_node_8_out_4, cmp_node_9_out_4, cmp_node_10_out_4);

  // Notes on the sheet:
  //   сравнитель 10 битных чисел
  //   числа вводятся с старших разрядов по очереди
  //   выдает 1 если второе больше первого
endmodule

module cmp_node (
  input  in_1,
  input  in_2,
  input  in_3,
  output out_4,
  output out_5
);

  wire and_2_out, not_1_out, not_2_out, not_3_out, not_4_out;

  not not_1 (not_1_out, in_2);
  not not_2 (not_2_out, in_1);
  and and_1 (out_4, not_1_out, not_2_out, in_3);
  not not_3 (not_3_out, in_3);
  and and_2 (and_2_out, not_3_out, not_4_out, in_2);
  not not_4 (not_4_out, in_1);
  or or_1 (out_5, and_2_out, out_4, in_1);

  // Notes on the sheet:
  //   сравнились ли уже числа
  //   результат сравнения 
  //   сравнились ли числа сейчас
endmodule

module next_sqrt_bit (
  input  in_1,
  input  in_2,
  input  in_3,
  input  in_4,
  input  in_5,
  input  in_6,
  input  in_7,
  input  in_8,
  input  in_9,
  input  in_10,
  input  in_11,
  input  in_12,
  input  in_13,
  input  in_14,
  input  in_15,
  input  in_16,
  output out_17,
  output out_18,
  output out_19,
  output out_20,
  output out_21,
  output out_22,
  output out_23,
  output out_24
);

  wire cmp_1_out_21, sqr_1_out_6, sqr_1_out_7, sqr_1_out_8, sqr_1_out_9, sqr_1_out_10, sqr_1_out_11,
       sqr_1_out_12, sqr_1_out_13, sqr_1_out_14, sqr_1_out_15;

  not not_1 (out_17, 1'b1);
  sqr sqr_1 (
    .in_1(in_13), .in_2(in_14), .in_3(in_15), .in_4(in_16), .in_5(1'b1), .out_6(sqr_1_out_6),
    .out_7(sqr_1_out_7), .out_8(sqr_1_out_8), .out_9(sqr_1_out_9), .out_10(sqr_1_out_10),
    .out_11(sqr_1_out_11), .out_12(sqr_1_out_12), .out_13(sqr_1_out_13), .out_14(sqr_1_out_14),
    .out_15(sqr_1_out_15));
  cmp cmp_1 (
    .in_1(out_17), .in_2(sqr_1_out_6), .in_3(out_17), .in_4(sqr_1_out_7), .in_5(in_1), .in_6(sqr_1_out_8),
    .in_7(in_2), .in_8(sqr_1_out_9), .in_9(in_3), .in_10(sqr_1_out_10), .in_11(in_4), .in_12(sqr_1_out_11),
    .in_13(in_5), .in_14(sqr_1_out_12), .in_15(in_7), .in_16(sqr_1_out_13), .in_17(in_9),
    .in_18(sqr_1_out_14), .in_19(in_11), .in_20(sqr_1_out_15), .out_21(cmp_1_out_21));
  not not_2 (out_24, cmp_1_out_21);

  assign out_18 = out_17;
  assign out_19 = out_17;
  assign out_20 = in_13;
  assign out_21 = in_14;
  assign out_22 = in_15;
  assign out_23 = in_16;
endmodule

module sum_node (
  input  in_1,
  input  in_2,
  input  in_3,
  output out_4,
  output out_5
);

  wire and_1_out, and_2_out, or_1_out;

  xor xor_1 (out_4, in_1, in_2, in_3);
  or or_1 (or_1_out, in_3, in_2);
  and and_1 (and_1_out, in_3, in_2);
  and and_2 (and_2_out, in_1, or_1_out);
  or or_2 (out_5, and_2_out, and_1_out);
endmodule

module sum (
  input  in_1,
  input  in_2,
  input  in_3,
  input  in_4,
  input  in_5,
  input  in_6,
  input  in_7,
  input  in_8,
  input  in_9,
  input  in_10,
  input  in_11,
  input  in_12,
  input  in_13,
  input  in_14,
  input  in_15,
  input  in_16,
  input  in_17,
  input  in_18,
  input  in_19,
  input  in_20,
  output out_21,
  output out_22,
  output out_23,
  output out_24,
  output out_25,
  output out_26,
  output out_27,
  output out_28,
  output out_29,
  output out_30
);

  wire not_1_out, sum_node_1_out_5, sum_node_2_out_5, sum_node_3_out_5, sum_node_4_out_5, sum_node_5_out_5,
       sum_node_6_out_5, sum_node_7_out_5, sum_node_8_out_5, sum_node_9_out_5;

  not not_1 (not_1_out, 1'b1);
  sum_node sum_node_1 (.in_1(not_1_out), .in_2(in_1), .in_3(in_2), .out_4(out_21), .out_5(sum_node_1_out_5));
  sum_node sum_node_2 (.in_1(sum_node_1_out_5), .in_2(in_3), .in_3(in_4), .out_4(out_22), .out_5(sum_node_2_out_5));
  sum_node sum_node_3 (.in_1(sum_node_2_out_5), .in_2(in_5), .in_3(in_6), .out_4(out_23), .out_5(sum_node_3_out_5));
  sum_node sum_node_4 (.in_1(sum_node_3_out_5), .in_2(in_7), .in_3(in_8), .out_4(out_24), .out_5(sum_node_4_out_5));
  sum_node sum_node_5 (.in_1(sum_node_4_out_5), .in_2(in_9), .in_3(in_10), .out_4(out_25), .out_5(sum_node_5_out_5));
  sum_node sum_node_6 (.in_1(sum_node_5_out_5), .in_2(in_11), .in_3(in_12), .out_4(out_26), .out_5(sum_node_6_out_5));
  sum_node sum_node_7 (.in_1(sum_node_6_out_5), .in_2(in_13), .in_3(in_14), .out_4(out_27), .out_5(sum_node_7_out_5));
  sum_node sum_node_8 (.in_1(sum_node_7_out_5), .in_2(in_15), .in_3(in_16), .out_4(out_28), .out_5(sum_node_8_out_5));
  sum_node sum_node_9 (.in_1(sum_node_8_out_5), .in_2(in_17), .in_3(in_18), .out_4(out_29), .out_5(sum_node_9_out_5));
  sum_node sum_node_10 (.in_1(sum_node_9_out_5), .in_2(in_19), .in_3(in_20), .out_4(out_30));  // open: out_5
endmodule

module sqr_node (
  input  in_1,
  input  in_2,
  input  in_3,
  input  in_4,
  input  in_5,
  input  in_6,
  output out_7,
  output out_8,
  output out_9,
  output out_10,
  output out_11
);

  and and_1 (out_7, in_1, in_2);
  and and_2 (out_8, in_1, in_3);
  and and_3 (out_9, in_1, in_4);
  and and_4 (out_10, in_1, in_5);
  and and_5 (out_11, in_6, in_1);
endmodule

module sqr (
  input  in_1,
  input  in_2,
  input  in_3,
  input  in_4,
  input  in_5,
  output out_6,
  output out_7,
  output out_8,
  output out_9,
  output out_10,
  output out_11,
  output out_12,
  output out_13,
  output out_14,
  output out_15
);

  wire not_1_out, sqr_node_1_out_7, sqr_node_1_out_8, sqr_node_1_out_9, sqr_node_1_out_10, sqr_node_1_out_11,
       sqr_node_2_out_7, sqr_node_2_out_8, sqr_node_2_out_9, sqr_node_2_out_10, sqr_node_2_out_11,
       sqr_node_3_out_7, sqr_node_3_out_8, sqr_node_3_out_9, sqr_node_3_out_10, sqr_node_3_out_11,
       sqr_node_4_out_7, sqr_node_4_out_8, sqr_node_4_out_9, sqr_node_4_out_10, sqr_node_4_out_11,
       sqr_node_5_out_7, sqr_node_5_out_8, sqr_node_5_out_9, sqr_node_5_out_10, sqr_node_5_out_11,
       sum_1_out_21, sum_1_out_22, sum_1_out_23, sum_1_out_24, sum_1_out_25, sum_1_out_26, sum_1_out_28,
       sum_1_out_29, sum_1_out_30, sum_2_out_21, sum_2_out_22, sum_2_out_23, sum_2_out_24, sum_2_out_25,
       sum_2_out_26, sum_2_out_27, sum_2_out_28, sum_2_out_29, sum_2_out_30, sum_3_out_21, sum_3_out_22,
       sum_3_out_23, sum_3_out_24, sum_3_out_25, sum_3_out_26, sum_3_out_27, sum_3_out_28, sum_3_out_29,
       sum_3_out_30, sum_4_out_21, sum_4_out_22, sum_4_out_23, sum_4_out_24, sum_4_out_25, sum_4_out_26,
       sum_4_out_27, sum_4_out_28, sum_4_out_29, sum_4_out_30;

  not not_1 (not_1_out, 1'b1);
  sqr_node sqr_node_1 (
    .in_1(in_5), .in_2(in_1), .in_3(in_2), .in_4(in_3), .in_5(in_4), .in_6(in_5), .out_7(sqr_node_1_out_7),
    .out_8(sqr_node_1_out_8), .out_9(sqr_node_1_out_9), .out_10(sqr_node_1_out_10), .out_11(sqr_node_1_out_11));
  sqr_node sqr_node_2 (
    .in_1(in_4), .in_2(in_1), .in_3(in_2), .in_4(in_3), .in_5(in_4), .in_6(in_5), .out_7(sqr_node_2_out_7),
    .out_8(sqr_node_2_out_8), .out_9(sqr_node_2_out_9), .out_10(sqr_node_2_out_10), .out_11(sqr_node_2_out_11));
  sqr_node sqr_node_3 (
    .in_1(in_3), .in_2(in_1), .in_3(in_2), .in_4(in_3), .in_5(in_4), .in_6(in_5), .out_7(sqr_node_3_out_7),
    .out_8(sqr_node_3_out_8), .out_9(sqr_node_3_out_9), .out_10(sqr_node_3_out_10), .out_11(sqr_node_3_out_11));
  sqr_node sqr_node_4 (
    .in_1(in_2), .in_2(in_1), .in_3(in_2), .in_4(in_3), .in_5(in_4), .in_6(in_5), .out_7(sqr_node_4_out_7),
    .out_8(sqr_node_4_out_8), .out_9(sqr_node_4_out_9), .out_10(sqr_node_4_out_10), .out_11(sqr_node_4_out_11));
  sqr_node sqr_node_5 (
    .in_1(in_1), .in_2(in_1), .in_3(in_2), .in_4(in_3), .in_5(in_4), .in_6(in_5), .out_7(sqr_node_5_out_7),
    .out_8(sqr_node_5_out_8), .out_9(sqr_node_5_out_9), .out_10(sqr_node_5_out_10), .out_11(sqr_node_5_out_11));
  sum sum_1 (
    .in_1(not_1_out), .in_2(sqr_node_1_out_11), .in_3(not_1_out), .in_4(sqr_node_1_out_10), .in_5(not_1_out),
    .in_6(sqr_node_1_out_9), .in_7(not_1_out), .in_8(sqr_node_1_out_8), .in_9(not_1_out),
    .in_10(sqr_node_1_out_7), .in_11(not_1_out), .in_12(not_1_out), .in_13(not_1_out), .in_14(not_1_out),
    .in_15(not_1_out), .in_16(not_1_out), .in_17(not_1_out), .in_18(not_1_out), .in_19(not_1_out),
    .in_20(not_1_out), .out_21(sum_1_out_21), .out_22(sum_1_out_22), .out_23(sum_1_out_23),
    .out_24(sum_1_out_24), .out_25(sum_1_out_25), .out_26(sum_1_out_26), .out_27(sum_1_out_26),
    .out_28(sum_1_out_28), .out_29(sum_1_out_29), .out_30(sum_1_out_30));
  sum sum_2 (
    .in_1(not_1_out), .in_2(sum_1_out_21), .in_3(sqr_node_2_out_11), .in_4(sum_1_out_22),
    .in_5(sqr_node_2_out_10), .in_6(sum_1_out_23), .in_7(sqr_node_2_out_9), .in_8(sum_1_out_24),
    .in_9(sqr_node_2_out_8), .in_10(sum_1_out_25), .in_11(sqr_node_2_out_7), .in_12(sum_1_out_26),
    .in_13(not_1_out), .in_14(sum_1_out_26), .in_15(not_1_out), .in_16(sum_1_out_28), .in_17(not_1_out),
    .in_18(sum_1_out_29), .in_19(not_1_out), .in_20(sum_1_out_30), .out_21(sum_2_out_21),
    .out_22(sum_2_out_22), .out_23(sum_2_out_23), .out_24(sum_2_out_24), .out_25(sum_2_out_25),
    .out_26(sum_2_out_26), .out_27(sum_2_out_27), .out_28(sum_2_out_28), .out_29(sum_2_out_29),
    .out_30(sum_2_out_30));
  sum sum_3 (
    .in_1(not_1_out), .in_2(sum_2_out_21), .in_3(not_1_out), .in_4(sum_2_out_22), .in_5(sqr_node_3_out_11),
    .in_6(sum_2_out_23), .in_7(sqr_node_3_out_10), .in_8(sum_2_out_24), .in_9(sqr_node_3_out_9),
    .in_10(sum_2_out_25), .in_11(sqr_node_3_out_8), .in_12(sum_2_out_26), .in_13(sqr_node_3_out_7),
    .in_14(sum_2_out_27), .in_15(not_1_out), .in_16(sum_2_out_28), .in_17(not_1_out), .in_18(sum_2_out_29),
    .in_19(not_1_out), .in_20(sum_2_out_30), .out_21(sum_3_out_21), .out_22(sum_3_out_22),
    .out_23(sum_3_out_23), .out_24(sum_3_out_24), .out_25(sum_3_out_25), .out_26(sum_3_out_26),
    .out_27(sum_3_out_27), .out_28(sum_3_out_28), .out_29(sum_3_out_29), .out_30(sum_3_out_30));
  sum sum_4 (
    .in_1(not_1_out), .in_2(sum_3_out_21), .in_3(not_1_out), .in_4(sum_3_out_22), .in_5(not_1_out),
    .in_6(sum_3_out_23), .in_7(sqr_node_4_out_11), .in_8(sum_3_out_24), .in_9(sqr_node_4_out_10),
    .in_10(sum_3_out_25), .in_11(sqr_node_4_out_9), .in_12(sum_3_out_26), .in_13(sqr_node_4_out_8),
    .in_14(sum_3_out_27), .in_15(sqr_node_4_out_7), .in_16(sum_3_out_28), .in_17(not_1_out),
    .in_18(sum_3_out_29), .in_19(not_1_out), .in_20(sum_3_out_30), .out_21(sum_4_out_21),
    .out_22(sum_4_out_22), .out_23(sum_4_out_23), .out_24(sum_4_out_24), .out_25(sum_4_out_25),
    .out_26(sum_4_out_26), .out_27(sum_4_out_27), .out_28(sum_4_out_28), .out_29(sum_4_out_29),
    .out_30(sum_4_out_30));
  sum sum_5 (
    .in_1(not_1_out), .in_2(sum_4_out_21), .in_3(not_1_out), .in_4(sum_4_out_22), .in_5(not_1_out),
    .in_6(sum_4_out_23), .in_7(not_1_out), .in_8(sum_4_out_24), .in_9(sqr_node_5_out_11),
    .in_10(sum_4_out_25), .in_11(sqr_node_5_out_10), .in_12(sum_4_out_26), .in_13(sqr_node_5_out_9),
    .in_14(sum_4_out_27), .in_15(sqr_node_5_out_8), .in_16(sum_4_out_28), .in_17(sqr_node_5_out_7),
    .in_18(sum_4_out_29), .in_19(sum_4_out_30), .in_20(sum_4_out_30), .out_21(out_15), .out_22(out_14),
    .out_23(out_13), .out_24(out_12), .out_25(out_11), .out_26(out_10), .out_27(out_9), .out_28(out_8),
    .out_29(out_7), .out_30(out_6));
endmodule
